// Logisim project Architecture.circ as structural Verilog: 2 circuits, main circuit main
module main (
  input  [7:0] A,
  input  [7:0] B,
  input  [1:0] \Opération ,
  input  in_4,
  output out_5,
  output [7:0] out_6
);

  wire adder_1_cout, adder_2_cout, comparator_1_gt;
  wire [7:0] adder_1_out, adder_2_out, divider_1_out, divider_1_rem, multiplier_1_cout, multiplier_1_out,
       negator_1_out;

  // Probe on A
  // Probe on B
  Negator negator_1 (.in(B), .out(negator_1_out));
  // Probe on A
  // Probe on B
  // Probe on divider_1_rem
  Adder adder_1 (.a(A), .b(B), .out(adder_1_out), .cout(adder_1_cout));  // open: cin
  Adder adder_2 (.a(A), .b(negator_1_out), .out(adder_2_out), .cout(adder_2_cout));  // open: cin
  Multiplier multiplier_1 (.a(A), .b(B), .out(multiplier_1_out), .cout(multiplier_1_cout));  // open: cin
  Divider divider_1 (.a(A), .b(B), .out(divider_1_out), .rem(divider_1_rem));  // open: upper
  Multiplexer #(.select(2), .width(8)) multiplexer_1 (
    .in0(adder_1_out), .in1(adder_2_out), .in2(multiplier_1_out), .in3(divider_1_out), .out(out_6),
    .sel(\Opération ), .en(in_4));
  // Probe on out_6
  Comparator comparator_1 (.a(multiplier_1_cout), .b({8{1'b0}}), .gt(comparator_1_gt));  // open: eq, lt
  Multiplexer #(.select(2)) multiplexer_2 (
    .in0(adder_1_cout), .in2(adder_2_cout), .in3(comparator_1_gt), .out(out_5), .sel(\Opération ), .en(in_4));  // open: in1
endmodule

module valeurAbsolu (
  input  [7:0] Entree,
  output [7:0] Sortie
);

  wire bitselector_1_out;
  wire [7:0] negator_1_out;

  // Probe on Entree
  BitSelector bitselector_1 (.in(Entree), .out(bitselector_1_out), .sel(3'b111));
  // Probe on Sortie
  Negator negator_1 (.in(Entree), .out(negator_1_out));
  Multiplexer #(.width(8), .enable("false")) multiplexer_1 (
    .in0(Entree), .in1(negator_1_out), .out(Sortie), .sel(bitselector_1_out));
endmodule
