// Logisim project PROJET-BON.circ as structural Verilog: 2 circuits, main circuit main
module main (
  input  Activation
);

  wire clock_1_out, comparator_1_eq, comparator_2_eq, comparator_3_eq, comparator_3_gt, comparator_4_eq,
       controlled_buffer_1_out, counter_2_q, j_k_ff_1_q, not_1_out, not_2_out, not_3_out, not_4_out,
       not_5_out, or_1_out, \unité_calcul_1_debordement ;
  wire [1:0] bitselector_1_out;
  wire [7:0] controlled_buffer_2_out, controlled_buffer_3_out, controlled_buffer_4_out,
       controlled_buffer_5_out, controlled_buffer_6_out, controlled_buffer_8_out, controlled_buffer_9_out,
       counter_1_q, register_1_q, register_2_q, register_3_q, rom_1_data, subtractor_1_out,
       \unité_calcul_1_sortie ;

  Clock clock_1 (.out(clock_1_out));
  assign controlled_buffer_1_out = not_1_out ? clock_1_out : 1'bz;  // Controlled_Buffer controlled_buffer_1
  not not_1 (not_1_out, comparator_3_eq);
  // Probe on counter_1_q
  Counter counter_1 (.Q(counter_1_q), .clk(controlled_buffer_1_out));  // open: load, D, count, carry, clr
  Comparator comparator_1 (.a({8{1'b0}}), .b(counter_1_q), .eq(comparator_1_eq));  // open: gt, lt
  // Probe on counter_1_q
  Comparator comparator_2 (.a({8{1'b0}}), .b(counter_1_q), .eq(comparator_2_eq));  // open: gt, lt
  ROM rom_1 (.addr(counter_1_q), .data(rom_1_data));  // open: sel
  J_K_Flip_Flop j_k_ff_1 (
    .J(1'b1), .clk(controlled_buffer_1_out), .K(1'b1), .Q(j_k_ff_1_q));  // open: Qn, preset, en, reset
  not not_2 (not_2_out, comparator_2_eq);
  assign controlled_buffer_2_out = comparator_3_gt ? rom_1_data : 8'bz;  // Controlled_Buffer controlled_buffer_2
  Comparator comparator_3 (.a(rom_1_data), .b({8{1'b0}}), .gt(comparator_3_gt), .eq(comparator_3_eq));  // open: lt
  assign controlled_buffer_3_out = not_3_out ? controlled_buffer_2_out : 8'bz;  // Controlled_Buffer controlled_buffer_3
  not not_3 (not_3_out, j_k_ff_1_q);
  assign controlled_buffer_4_out = j_k_ff_1_q ? controlled_buffer_2_out : 8'bz;  // Controlled_Buffer controlled_buffer_4
  not not_4 (not_4_out, comparator_2_eq);
  or or_1 (or_1_out, comparator_1_eq, not_2_out);
  assign controlled_buffer_5_out = j_k_ff_1_q ? controlled_buffer_9_out : 8'bz;  // Controlled_Buffer controlled_buffer_5
  assign controlled_buffer_6_out = not_5_out ? controlled_buffer_3_out : 8'bz;  // Controlled_Buffer controlled_buffer_6
  not not_5 (not_5_out, comparator_2_eq);
  assign controlled_buffer_5_out = comparator_2_eq ? controlled_buffer_2_out : 8'bz;  // Controlled_Buffer controlled_buffer_7
  assign controlled_buffer_8_out = not_4_out ? controlled_buffer_4_out : 8'bz;  // Controlled_Buffer controlled_buffer_8
  Register register_1 (.D(controlled_buffer_6_out), .Q(register_1_q), .clk(controlled_buffer_1_out));  // open: en, clr
  Register register_2 (.D(controlled_buffer_8_out), .Q(register_2_q), .clk(controlled_buffer_1_out));  // open: en, clr
  assign controlled_buffer_9_out = or_1_out ? \unité_calcul_1_sortie  : 8'bz;  // Controlled_Buffer controlled_buffer_9
  // Probe on register_1_q
  Register register_3 (.D(controlled_buffer_5_out), .Q(register_3_q), .clk(controlled_buffer_1_out));  // open: en, clr
  Subtractor subtractor_1 (.a(register_2_q), .b(8'h1), .out(subtractor_1_out));  // open: bin, bout
  // Probe on register_3_q
  BitSelector #(.group(2)) bitselector_1 (.in(subtractor_1_out), .out(bitselector_1_out), .sel(2'b00));
  // Probe on bitselector_1_out
  // Probe on \unité_calcul_1_sortie 
  Counter #(.width(1), .max('h1)) counter_2 (
    .count(comparator_4_eq), .Q(counter_2_q), .clk(clock_1_out));  // open: load, D, carry, clr
  Comparator #(.width(1)) comparator_4 (
    .a(\unité_calcul_1_debordement ), .b(1'b1), .eq(comparator_4_eq));  // open: gt, lt
  \unité_calcul  \unité_calcul_1  (
    .A(register_3_q), .B(register_1_q), .Code(bitselector_1_out), .Sortie(\unité_calcul_1_sortie ),
    .Debordement(\unité_calcul_1_debordement ), .E(Activation));
  LED led_1 (.in(counter_2_q));

  // Notes on the sheet:
  //   contents of rom_1 (hex, n*v repeats v):
  //   5 3 c 1 11 4 2 2 16
  //   Résultat
  //   Débordement
endmodule

module \unité_calcul  (
  input  [7:0] A,
  input  [7:0] B,
  input  [1:0] Code,
  input  E,
  output [7:0] Sortie,
  output Debordement
);

  wire adder_1_cout, comparator_1_gt, comparator_1_lt, comparator_2_gt, not_1_out, not_2_out;
  wire [7:0] adder_1_out, controlled_buffer_1_out, controlled_buffer_3_out, divider_1_out, divider_1_rem,
       multiplier_1_cout, multiplier_1_out, subtractor_1_out;

  // Probe on A
  // Probe on B
  not not_1 (not_1_out, comparator_1_gt);
  Comparator #(.mode("unsigned")) comparator_1 (.a(A), .b(B), .gt(comparator_1_gt), .lt(comparator_1_lt));  // open: eq
  Multiplier multiplier_1 (.a(A), .b(B), .out(multiplier_1_out), .cout(multiplier_1_cout));  // open: cin
  // Probe on divider_1_rem
  assign controlled_buffer_1_out = comparator_1_gt ? A : 8'bz;  // Controlled_Buffer controlled_buffer_1
  assign controlled_buffer_1_out = not_1_out ? B : 8'bz;  // Controlled_Buffer controlled_buffer_2
  Divider divider_1 (.a(A), .b(B), .out(divider_1_out), .rem(divider_1_rem));  // open: upper
  // Probe on controlled_buffer_1_out
  assign controlled_buffer_3_out = not_2_out ? B : 8'bz;  // Controlled_Buffer controlled_buffer_3
  assign controlled_buffer_3_out = comparator_1_lt ? A : 8'bz;  // Controlled_Buffer controlled_buffer_4
  not not_2 (not_2_out, comparator_1_lt);
  Comparator comparator_2 (.a(multiplier_1_cout), .b({8{1'b0}}), .gt(comparator_2_gt));  // open: eq, lt
  Subtractor subtractor_1 (
    .a(controlled_buffer_1_out), .b(controlled_buffer_3_out), .out(subtractor_1_out));  // open: bin, bout
  // Probe on subtractor_1_out
  // Probe on multiplier_1_out
  // Probe on comparator_2_gt
  // Probe on divider_1_out
  Adder adder_1 (.a(A), .b(B), .out(adder_1_out), .cout(adder_1_cout));  // open: cin
  // Probe on adder_1_cout
  // Probe on adder_1_out
  Multiplexer #(.select(2), .width(8)) multiplexer_1 (
    .in0(adder_1_out), .in1(subtractor_1_out), .in2(multiplier_1_out), .in3(divider_1_out), .out(Sortie),
    .sel(Code), .en(E));
  // Probe on Sortie
  Multiplexer #(.select(2)) multiplexer_2 (
    .in0(adder_1_cout), .in1(1'b0), .in2(comparator_2_gt), .in3(1'b0), .out(Debordement), .sel(Code), .en(E));
endmodule
